// Logisim project 10.27.circ as structural Verilog: 20 circuits, main circuit main
module main (
  input  in_1,
  input  in_2,
  input  A,
  input  in_4,
  input  B,
  output out_6,
  output out_7,
  output Carry,
  output Sum
);

  myAdder myadder_1 (.A(in_1), .B(in_2), .SUM(out_6), .Cin(in_4), .CARRYout(out_7));
  myAdder myadder_2 (.A(A), .B(1'b0), .SUM(Sum), .Cin(B), .CARRYout(Carry));
endmodule

module myAdder (
  input  A,
  input  B,
  input  Cin,
  output SUM,
  output CARRYout
);

  wire and_1_out, and_2_out, xor_1_out;

  xor xor_1 (xor_1_out, A, B);
  and and_1 (and_1_out, B, A);
  xor xor_2 (SUM, xor_1_out, Cin);
  and and_2 (and_2_out, xor_1_out, Cin);
  or or_1 (CARRYout, and_2_out, and_1_out);
endmodule

module _2bitAdder (
  input  A1,
  input  A0,
  input  B1,
  input  B0,
  output out_5,
  output out_6,
  output out_7
);

  wire myadder_2_carryout;

  myAdder myadder_1 (.A(A1), .B(B1), .SUM(out_6), .Cin(myadder_2_carryout), .CARRYout(out_5));
  myAdder myadder_2 (.A(A0), .B(B0), .SUM(out_7), .Cin(1'b0), .CARRYout(myadder_2_carryout));
endmodule

module _3bitAdder (
  input  A2,
  input  A1,
  input  A0,
  input  B2,
  input  B1,
  input  B0,
  output out_7,
  output out_8,
  output out_9,
  output out_10
);

  wire myadder_2_carryout, myadder_3_carryout;

  myAdder myadder_1 (.A(A2), .B(B2), .SUM(out_8), .Cin(myadder_2_carryout), .CARRYout(out_7));
  myAdder myadder_2 (.A(A1), .B(B1), .SUM(out_9), .Cin(myadder_3_carryout), .CARRYout(myadder_2_carryout));
  myAdder myadder_3 (.A(B0), .B(A0), .SUM(out_10), .Cin(1'b0), .CARRYout(myadder_3_carryout));
endmodule

module HA (
  input  A,
  input  B,
  output sum,
  output carry
);

  xor xor_1 (sum, A, B);
  and and_1 (carry, A, B);
endmodule

module _2_S (
  input  in_1,
  input  in_2,
  input  in_3,
  input  in_4,
  output out_5,
  output out_6,
  output out_7,
  output out_8,
  output out_9
);

  wire ha_2_carry, ha_3_carry, ha_4_carry, not_1_out, not_2_out, not_3_out, not_4_out;

  not not_1 (not_1_out, in_1);
  HA ha_1 (.A(ha_2_carry), .B(not_1_out), .sum(out_6), .carry(out_5));
  not not_2 (not_2_out, in_2);
  HA ha_2 (.A(ha_3_carry), .B(not_2_out), .sum(out_7), .carry(ha_2_carry));
  not not_3 (not_3_out, in_4);
  not not_4 (not_4_out, in_3);
  HA ha_3 (.A(ha_4_carry), .B(not_4_out), .sum(out_8), .carry(ha_3_carry));
  HA ha_4 (.A(1'b1), .B(not_3_out), .sum(out_9), .carry(ha_4_carry));
endmodule

module _1_s (
  input  in_1,
  input  in_2,
  input  in_3,
  input  in_4,
  input  in_5,
  output out_6,
  output out_7,
  output out_8,
  output out_9
);

  xor xor_1 (out_6, in_5, in_1);
  xor xor_2 (out_7, in_5, in_2);
  xor xor_3 (out_8, in_5, in_3);
  xor xor_4 (out_9, in_5, in_4);
endmodule

module _2_s_control (
  input  in_1,
  input  in_2,
  input  in_3,
  input  in_4,
  input  in_5,
  output out_6,
  output out_7,
  output out_8,
  output out_9,
  output out_10
);

  wire ha_2_carry, ha_3_carry, ha_4_carry, xor_1_out, xor_2_out, xor_3_out, xor_4_out;

  xor xor_1 (xor_1_out, in_5, in_1);
  HA ha_1 (.A(ha_2_carry), .B(xor_1_out), .sum(out_7), .carry(out_6));
  xor xor_2 (xor_2_out, in_5, in_2);
  HA ha_2 (.A(ha_3_carry), .B(xor_2_out), .sum(out_8), .carry(ha_2_carry));
  xor xor_3 (xor_3_out, in_5, in_3);
  HA ha_3 (.A(ha_4_carry), .B(xor_3_out), .sum(out_9), .carry(ha_3_carry));
  xor xor_4 (xor_4_out, in_5, in_4);
  HA ha_4 (.A(in_5), .B(xor_4_out), .sum(out_10), .carry(ha_4_carry));
endmodule

module negative (
  input  in_1,
  input  in_2,
  input  in_3,
  input  in_4,
  output out_5,
  output out_6,
  output out_7,
  output out_8,
  output out_9
);

  wire ha_2_carry, ha_3_carry, ha_4_carry, xor_1_out, xor_2_out, xor_3_out, xor_4_out;

  xor xor_1 (xor_1_out, in_1, in_1);
  HA ha_1 (.A(ha_2_carry), .B(xor_1_out), .sum(out_6), .carry(out_5));
  xor xor_2 (xor_2_out, in_1, in_2);
  HA ha_2 (.A(ha_3_carry), .B(xor_2_out), .sum(out_7), .carry(ha_2_carry));
  xor xor_3 (xor_3_out, in_1, in_3);
  HA ha_3 (.A(ha_4_carry), .B(xor_3_out), .sum(out_8), .carry(ha_3_carry));
  xor xor_4 (xor_4_out, in_1, in_4);
  HA ha_4 (.A(in_1), .B(xor_4_out), .sum(out_9), .carry(ha_4_carry));
endmodule

module _2_4decoder (
  input  in_1,
  input  in_2,
  output out_3,
  output out_4,
  output out_5,
  output out_6
);

  wire not_1_out, not_2_out, not_3_out, not_4_out;

  not not_1 (not_1_out, in_2);
  not not_2 (not_2_out, in_1);
  not not_3 (not_3_out, in_2);
  not not_4 (not_4_out, in_1);
  and _00 (out_3, not_1_out, not_2_out);
  and _01 (out_4, not_3_out, in_1);
  and _10 (out_5, in_2, not_4_out);
  and _11 (out_6, in_2, in_1);
endmodule

module _2_4decoder_2 (
  input  x0,
  input  x1,
  output out_3,
  output out_4,
  output out_5,
  output out_6
);

  wire not_1_out, not_2_out;

  not not_1 (not_1_out, x0);
  not not_2 (not_2_out, x1);
  and _00 (out_3, not_1_out, not_2_out);
  and _01 (out_4, not_2_out, x0);
  and _10 (out_5, not_1_out, x1);
  and _11 (out_6, x0, x1);

  // Notes on the sheet:
  //   x1x0
endmodule

module _4_2encoder (
  input  L0,
  input  L1,
  input  L2,
  input  L3,
  output X0,
  output X1,
  output out_7
);

  wire and_1_out, not_1_out;

  not not_1 (not_1_out, L2);
  and and_1 (and_1_out, L1, not_1_out);
  or or_1 (X1, L2, L3);
  or or_2 (out_7, L0, L3, L2, L1);
  or or_3 (X0, and_1_out, L3);
endmodule

module _4lineMux (
  input  in_1,
  input  in_2,
  input  in_3,
  input  in_4,
  input  in_5,
  input  in_6,
  output out_7
);

  wire and_1_out, and_2_out, and_3_out, and_4_out, not_1_out, not_2_out, not_3_out, not_4_out;

  not not_1 (not_1_out, in_1);
  not not_2 (not_2_out, in_2);
  not not_3 (not_3_out, in_1);
  not not_4 (not_4_out, in_2);
  and and_1 (and_1_out, not_1_out, not_2_out, in_3);
  and and_2 (and_2_out, not_3_out, in_2, in_4);
  and and_3 (and_3_out, in_1, not_4_out, in_5);
  and and_4 (and_4_out, in_2, in_1, in_6);
  or or_1 (out_7, and_1_out, and_2_out, and_3_out, and_4_out);
endmodule

module _4lineDemux (
  input  in_1,
  input  in_2,
  input  in_3,
  output out_4,
  output out_5,
  output out_6,
  output out_7
);

  wire not_1_out, not_2_out, not_3_out, not_4_out;

  not not_1 (not_1_out, in_1);
  not not_2 (not_2_out, in_2);
  not not_3 (not_3_out, in_1);
  not not_4 (not_4_out, in_2);
  and and_1 (out_4, not_1_out, not_2_out, in_3);
  and and_2 (out_5, not_3_out, in_2, in_3);
  and and_3 (out_6, in_1, not_4_out, in_3);
  and and_4 (out_7, in_2, in_1, in_3);
endmodule

module comparator (
  input  A,
  input  B,
  output out_3,
  output out_4,
  output out_5
);

  wire not_1_out, not_3_out, xor_1_out;

  not not_1 (not_1_out, A);
  and and_1 (out_3, not_1_out, B);
  xor xor_1 (xor_1_out, A, B);
  not not_2 (out_4, xor_1_out);
  not not_3 (not_3_out, B);
  and and_2 (out_5, A, not_3_out);
endmodule

module ALU (
  input  in_1,
  input  in_2,
  input  A,
  input  B,
  input  CIN,
  output OUTPUT,
  output COUT
);

  wire and_1_out, and_2_out, myadder_1_sum, n2linemux_1_out_4, not_1_out, or_1_out;

  not not_1 (not_1_out, B);
  _2lineMux u_2linemux_1 (.in_2(B), .in_3(not_1_out), .in_1(and_1_out), .out_4(n2linemux_1_out_4));
  and and_1 (and_1_out, in_1, in_2);
  and and_2 (and_2_out, A, B);
  or or_1 (or_1_out, A, B);
  myAdder myadder_1 (.A(A), .B(n2linemux_1_out_4), .SUM(myadder_1_sum), .Cin(CIN), .CARRYout(COUT));
  _4lineMux u_4linemux_1 (
    .in_3(and_2_out), .in_4(or_1_out), .in_5(myadder_1_sum), .in_6(myadder_1_sum), .in_1(in_1), .in_2(in_2),
    .out_7(OUTPUT));
endmodule

module _2lineMux (
  input  in_1,
  input  in_2,
  input  in_3,
  output out_4
);

  wire and_1_out, and_2_out, not_1_out;

  not not_1 (not_1_out, in_1);
  and and_1 (and_1_out, not_1_out, in_2);
  and and_2 (and_2_out, in_1, in_3);
  or or_1 (out_4, and_1_out, and_2_out);
endmodule

module _2bitALU (
);

  ALU alu_1 ();  // open: A, B, CIN, in_1, in_2, COUT, OUTPUT
  ALU alu_2 ();  // open: A, B, CIN, in_1, in_2, COUT, OUTPUT
endmodule

module _2bitcomparator (
  input  A1,
  input  A0,
  input  B1,
  input  B0,
  output A_B,
  output A_B_2,
  output A_B_3
);

  wire and_1_out, and_2_out, and_3_out, and_5_out, and_6_out, and_7_out, not_1_out, not_2_out, not_3_out,
       not_4_out, not_5_out, not_6_out, xor_1_out, xor_2_out;

  not not_1 (not_1_out, A1);
  and and_1 (and_1_out, not_1_out, B1);
  not not_2 (not_2_out, A0);
  and and_2 (and_2_out, not_2_out, B0);
  and and_3 (and_3_out, and_2_out, not_3_out);
  or or_1 (A_B_3, and_1_out, and_3_out);
  xor xor_1 (xor_1_out, A1, B1);
  not not_3 (not_3_out, xor_1_out);
  xor xor_2 (xor_2_out, A0, B0);
  not not_4 (not_4_out, xor_2_out);
  and and_4 (A_B, not_3_out, not_4_out);
  and and_5 (and_5_out, A1, not_5_out);
  not not_5 (not_5_out, B1);
  not not_6 (not_6_out, B0);
  and and_6 (and_6_out, A0, not_6_out);
  and and_7 (and_7_out, not_3_out, and_6_out);
  or or_2 (A_B_2, and_5_out, and_7_out);
endmodule

module _3bit_comparator (
  input  A2,
  input  A1,
  input  A0,
  input  B2,
  input  B1,
  input  B0,
  output A_B,
  output A_B_2,
  output A_B_3
);

  wire A0_B0_2_out, A0_B0_3_out, A0_B0_out, A1_B1_2_out, A1_B1_3_out, A1_B1_out, A2_B2_2_out, A2_B2_3_out,
       A2_B2_out, and_1_out, and_2_out, and_4_out, and_5_out, not_1_out, not_2_out, not_3_out, not_4_out,
       not_5_out, not_6_out, not_7_out, not_8_out, not_9_out;

  not not_1 (not_1_out, A2);
  and A2_B2 (A2_B2_out, not_1_out, B2);
  not not_2 (not_2_out, A1);
  and A1_B1 (A1_B1_out, not_2_out, B1);
  and and_1 (and_1_out, A1_B1_out, not_6_out);
  or or_1 (A_B_2, A2_B2_out, and_1_out, and_2_out);
  not not_3 (not_3_out, A0);
  and A0_B0 (A0_B0_out, not_3_out, B0);
  and and_2 (and_2_out, A0_B0_out, not_5_out, not_6_out);
  xor A0_B0_2 (A0_B0_2_out, A0, B0);
  xor A1_B1_2 (A1_B1_2_out, A1, B1);
  not not_4 (not_4_out, A0_B0_2_out);
  not not_5 (not_5_out, A1_B1_2_out);
  and and_3 (A_B, not_5_out, not_4_out, not_6_out);
  xor A2_B2_2 (A2_B2_2_out, A2, B2);
  not not_6 (not_6_out, A2_B2_2_out);
  not not_7 (not_7_out, B0);
  not not_8 (not_8_out, B2);
  and A2_B2_3 (A2_B2_3_out, not_8_out, A2);
  and A1_B1_3 (A1_B1_3_out, A1, not_9_out);
  and A0_B0_3 (A0_B0_3_out, not_7_out, A0);
  and and_4 (and_4_out, not_6_out, A1_B1_3_out);
  and and_5 (and_5_out, not_6_out, not_5_out, A0_B0_3_out);
  or or_2 (A_B_3, A2_B2_3_out, and_5_out, and_4_out);
  not not_9 (not_9_out, B1);
endmodule
