// Logisim project CS240_Zhang_Yuqian.circ as structural Verilog: 1 circuit, main circuit main
module main (
  input  A3,
  input  A2,
  input  A1,
  input  A0,
  input  B3,
  input  B2,
  input  B1,
  input  B0,
  output A_B,
  output A_B_2,
  output A_B_3
);

  wire A0_B0_2_out, A0_B0_3_out, A0_B0_out, A1_B1_2_out, A1_B1_3_out, A1_B1_out, A2_B2_2_out, A2_B2_3_out,
       A2_B2_out, A3_B3_2_out, A3_B3_3_out, A3_B3_out, and_1_out, and_2_out, and_3_out, and_5_out, and_6_out,
       and_7_out, not_1_out, not_2_out, not_3_out, not_4_out, not_5_out, not_6_out, not_7_out, not_8_out,
       not_9_out, not_10_out, not_11_out, not_12_out;

  not not_1 (not_1_out, B1);
  and A1_B1 (A1_B1_out, A1, not_1_out);
  and and_1 (and_1_out, A1_B1_out, not_5_out, not_6_out);
  not not_2 (not_2_out, B0);
  not not_3 (not_3_out, A3);
  and A0_B0 (A0_B0_out, A0, not_2_out);
  and A3_B3 (A3_B3_out, not_3_out, B3);
  and and_2 (and_2_out, not_5_out, A0_B0_out, not_6_out, not_7_out);
  or or_1 (A_B, and_2_out, and_1_out, and_3_out, A3_B3_out);
  not not_4 (not_4_out, B2);
  and A2_B2 (A2_B2_out, A2, not_4_out);
  and and_3 (and_3_out, A2_B2_out, not_6_out);
  xor A2_B2_2 (A2_B2_2_out, A2, B2);
  xor A3_B3_2 (A3_B3_2_out, A3, B3);
  not not_5 (not_5_out, A2_B2_2_out);
  not not_6 (not_6_out, A3_B3_2_out);
  xor A1_B1_2 (A1_B1_2_out, A1, B1);
  xor A0_B0_2 (A0_B0_2_out, A0, B0);
  not not_7 (not_7_out, A1_B1_2_out);
  not not_8 (not_8_out, A0_B0_2_out);
  and and_4 (A_B_2, not_6_out, not_5_out, not_7_out, not_8_out);
  not not_9 (not_9_out, A2);
  and A2_B2_3 (A2_B2_3_out, not_9_out, B2);
  and and_5 (and_5_out, not_6_out, A2_B2_3_out);
  not not_10 (not_10_out, A1);
  and A1_B1_3 (A1_B1_3_out, not_10_out, B1);
  and and_6 (and_6_out, not_5_out, not_6_out, A1_B1_3_out);
  or or_2 (A_B_3, and_6_out, and_5_out, and_7_out, A3_B3_3_out);
  not not_11 (not_11_out, A0);
  and A0_B0_3 (A0_B0_3_out, not_11_out, B0);
  and and_7 (and_7_out, not_5_out, not_7_out, not_6_out, A0_B0_3_out);
  not not_12 (not_12_out, B3);
  and A3_B3_3 (A3_B3_3_out, not_12_out, A3);
endmodule
